# Fritzing sketch Semaforo (saved by Fritzing 0.9.3b)
breadboards: 1

parts:
  LED1 = LED - 5mm [color="Green (565nm)" package="5 mm [THT]"]
  LED2 = LED - 5mm [color="Yellow (592nm)" package="5 mm [THT]"]
  LED3 = LED - 5mm [color="Red (633nm)" package="5 mm [THT]"]
  Componente1 = Arduino Uno (Rev3)

nets:
  N1: LED1.cathode, Componente1.D4
  N2: LED1.anode, LED2.anode, LED3.anode, Componente1.GND
  N3: LED2.cathode, Componente1.D3_PWM
  N4: LED3.cathode, Componente1.D2
