# Fritzing sketch Dimmer (saved by Fritzing 0.9.3b)
breadboards: 1

parts:
  LED3 = LED - 5mm [color="Red (633nm)" package="5 mm [THT]"]
  Componente1 = Arduino Uno (Rev3)

nets:
  N1: LED3.cathode, Componente1.D3_PWM
  N2: LED3.anode, Componente1.GND
