# Fritzing sketch Medidor de distancia (saved by Fritzing 0.9.3b)
breadboards: 1

parts:
  Componente1 = Arduino Uno (Rev3)
  hc-sr1 = hc-sr04
  LED1 = smd LED [color="Green (555nm)" package="0603 [SMD]"]
  LED2 = smd LED [color="Yellow (595nm)" package="0603 [SMD]"]
  LED3 = smd LED [color="Red (633nm)" package="0603 [SMD]"]

nets:
  N1: Componente1.D8, LED1.anode
  N2: Componente1.D9_PWM, LED2.anode
  N3: Componente1.D10_PWM/SS, LED3.anode
  N4: Componente1.D2, hc-sr1.Trig
  N5: Componente1.D3_PWM, hc-sr1.Echo
  5V: Componente1.5V, hc-sr1.VCC
  GND: Componente1.GND, hc-sr1.GND, LED1.cathode, LED2.cathode, LED3.cathode
